# Fritzing sketch SmArtRoom-insurance (saved by Fritzing 0.9.9b)
breadboards: 2

parts:
  Argon1 = Particle Argon
  Part1 = 12 NeoPixel Ring [part_number=1643]

nets:
  GND: Argon1.GND, Part1.GND
  N1: Argon1.D2, Part1.IN
  N2: Argon1.VUSB, Part1.VDD

custom parts:
  Particle Argon: The Argon is a powerful Wi-Fi enabled development board that can act as either a standalone Wi-Fi endpoint or Wi-Fi enabled gateway for Particle Mesh networks. It is based on the Nordic nRF52840 and has built-in battery charging circuitry so it’s easy to connect a Li-Po and deploy your local network in minutes. The Argon is great for connecting existing projects to the Particle Device Cloud or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
  12 NeoPixel Ring: 12 ultra bright smart LED NeoPixels are arranged in a circle with 1.5" (37mm) outer diameter. The rings are 'chainable' - connect the output pin of one to the input pin of another. Use only one microcontroller pin to control as many as you can chain together! Each LED is addressable as the driver chip is inside the LED. Each one has ~18mA constant current drive so the color will be very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
