# Fritzing sketch SmArtRoom-museum (saved by Fritzing 0.9.9b)
breadboards: 2

parts:
  Argon1 = Particle Argon
  M1 = BMP280
  LED2 = RGB LED (com. anode, rbg) [package="5 mm [THT]"]
  S1 = Pushbutton [package="[THT]"]
  R1 = Resistor [tolerance=±5% resistance=10k package="2010 [SMD]"]
  OLED_I2C1 = OLED 128x64 I2C Monochrome Display

nets:
  3.3V: Argon1.3.3V, M1.VIN, LED2.common_anode, S1.Pin_3, S1.Pin_4, OLED_I2C1.VDD
  GND: Argon1.GND, M1.GND, R1.Pin_0, OLED_I2C1.GND
  N1: Argon1.SDA, M1.SDA, OLED_I2C1.SDA
  N2: Argon1.SCL, M1.SCL, OLED_I2C1.SCK
  N3: Argon1.D3, LED2.green_cathode
  N4: Argon1.D4, LED2.red_cathode
  N5: Argon1.D5, LED2.blue_cathode
  N6: Argon1.D6, S1.Pin_1, S1.Pin_2, R1.Pin_1

custom parts:
  Particle Argon: The Argon is a powerful Wi-Fi enabled development board that can act as either a standalone Wi-Fi endpoint or Wi-Fi enabled gateway for Particle Mesh networks. It is based on the Nordic nRF52840 and has built-in battery charging circuitry so it’s easy to connect a Li-Po and deploy your local network in minutes. The Argon is great for connecting existing projects to the Particle Device Cloud or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
  BMP280: Temperature Humidity Barometric presure Sensor, I2C
  Pushbutton: A generic pushbutton.
